# Fritzing sketch wiring (saved by Fritzing 0.9.3b)

parts:
  LCD2004-I2C1 = LCD2004-I2C
  U1 = ESP32S-HiLetgo [part_number=ESP32S-HiLetgo]
  L1 = Solenoid
  L2 = Solenoid
  HLK-PM1 = HLK-PM12 [part_number=HLK-PM12]
  U2 = LM2596 step down module
  D1 = Rectifier Diode [part_number=1N4001 package="300 mil [THT]"]
  D2 = Rectifier Diode [part_number=1N4001 package="300 mil [THT]"]
  A1 = 2-Channel 5v Relay Shield [package=relay-2ch5v10a]
  J1 = Piezo Speaker

nets:
  GND: LCD2004-I2C1.GND, U1.GND, L1.pin1, L2.pin1, HLK-PM1.-Vo, U2.IN-, U2.OUT-, D1.cathode, D2.cathode, A1.Pin_1, A1.Pin_4, A1.Pin_10, J1.pin1
  VCC: LCD2004-I2C1.VCC, U1.VIN, U2.OUT+, A1.Pin_13
  N1: LCD2004-I2C1.SDA, U1.GPIO22
  N2: LCD2004-I2C1.SCL, U1.GPIO21
  N3: U1.GPIO18, A1.Pin_12
  N4: U1.GPIO19, A1.Pin_11
  N5: U1.GPIO23, J1.pin2
  N6: HLK-PM1.+Vo, U2.IN+, A1.Pin_2, A1.Pin_5

custom parts:
  LCD2004-I2C: A standard character display with 4x20 characters. Comes in many colors with LCM2004 IIC attached.
  ESP32S-HiLetgo: HiLetgo ESP-WROOM-32 ESP32 ESP-32S Development Board 2.4GHz Dual-Mode WiFi + Bluetooth Dual Cores Microcontroller The ESP32 integrated with Antenna switches, RF Balun, power amplifiers, low-noise amplifiers, filters, and management modules, and the entire solution occupies the least area of PCB. 2.4 GHz Wi-Fi plus Bluetooth dual-mode chip, with TSMC Ultra-low power consumption 40nm technology,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
  LM2596 step down module: LM2596 DC-DC step down power supply module 3 A.
  2-Channel 5v Relay Shield: 2 Channel 5v Relay Shield w. 2x SPD-06VDC-SD-C
